// Digital circuit alu.dig as structural Verilog
module alu (
  input  [63:0] A,
  input  [63:0] B,
  input  [2:0] OP,
  output [63:0] R
);

  wire [63:0] add_1_s, mul_1_mul, SLL_out, SRL_out, sub_1_s;

  Multiplexer #(.Selector_Bits(3), .Bits(64)) multiplexer_1 (
    .sel(OP), .in_0(add_1_s), .in_1(sub_1_s), .in_2(mul_1_mul), .in_3(SLL_out), .in_4(SRL_out),
    .in_5({64{1'b0}}), .in_6({64{1'b0}}), .in_7({64{1'b0}}), .out(R));
  Add #(.Bits(64)) add_1 (.a(A), .b(B), .c_i(1'b0), .s(add_1_s));  // open: c_o
  Sub #(.Bits(64)) sub_1 (.a(A), .b(B), .c_i(1'b0), .s(sub_1_s));  // open: c_o
  Mul #(.Bits(32)) mul_1 (.a(A[31:0]), .b(B[31:0]), .mul(mul_1_mul));
  BarrelShifter #(.Bits(64)) SLL (.in(A), .shift({1'b0, B[5:0]}), .out(SLL_out));
  BarrelShifter #(.Bits(64), .direction("right")) SRL (.in(A), .shift({1'b0, B[5:0]}), .out(SRL_out));
endmodule
