// Digital circuit inst-decoder.dig as structural Verilog
module inst_decoder (
  input  [31:0] IW,
  output RFW,
  output WDsel,
  output [1:0] PCsel,
  output [2:0] ALUSrcB,
  output ALUSrcA,
  output [2:0] ALUOp
);

  wire ADDI_eq, ADDR_eq, jal_eq_1_eq, jalr_eq_1_eq, LUI_eq, MUL_eq, SLLI_eq, SLLR_eq, SRLI_eq, SRLR_eq;
  wire [3:0] priorityencoder_1_num;

  opcode_funct3_funct7_eq ADDR (
    .iw_opcode(IW[6:0]), .iw_funct3(IW[14:12]), .iw_funct7(IW[31:25]), .funct7({7{1'b0}}),
    .opcode(7'b0110011), .funct3(3'b000), .eq(ADDR_eq));
  opcode_funct3_funct7_eq MUL (
    .iw_opcode(IW[6:0]), .iw_funct3(IW[14:12]), .iw_funct7(IW[31:25]), .funct7(7'b0000001),
    .opcode(7'b0110011), .funct3(3'b000), .eq(MUL_eq));
  opcode_funct3_eq SLLR (
    .iw_opcode(IW[6:0]), .iw_funct3(IW[14:12]), .funct3(3'b001), .opcode(7'b0110011), .eq(SLLR_eq));
  opcode_funct3_eq SRLR (
    .iw_opcode(IW[6:0]), .iw_funct3(IW[14:12]), .funct3(3'b101), .opcode(7'b0110011), .eq(SRLR_eq));
  opcode_funct3_eq ADDI (
    .opcode(IW[6:0]), .funct3(IW[14:12]), .iw_funct3(3'b000), .iw_opcode(7'b0010011), .eq(ADDI_eq));
  opcode_funct3_funct7_eq SLLI (
    .iw_opcode(IW[6:0]), .iw_funct3(IW[14:12]), .iw_funct7(IW[31:25]), .funct7({7{1'b0}}),
    .opcode(7'b0010011), .funct3(3'b001), .eq(SLLI_eq));
  opcode_funct3_funct7_eq SRLI (
    .iw_opcode(IW[6:0]), .iw_funct3(IW[14:12]), .iw_funct7(IW[31:25]), .funct7({7{1'b0}}),
    .opcode(7'b0010011), .funct3(3'b101), .eq(SRLI_eq));
  jal_eq jal_eq_1 (.opcode(IW[6:0]), .eq(jal_eq_1_eq));
  Comparator #(.Bits(7)) LUI (.a(IW[6:0]), .b(7'b0110111), .eq(LUI_eq));  // open: gt, lt
  jalr_eq jalr_eq_1 (.opcode(IW[6:0]), .funct3(IW[14:12]), .eq(jalr_eq_1_eq));
  PriorityEncoder #(.Selector_Bits(4)) priorityencoder_1 (
    .in0(ADDR_eq), .in1(MUL_eq), .in2(SLLR_eq), .in3(SRLR_eq), .in4(ADDI_eq), .in5(SLLI_eq), .in6(SRLI_eq),
    .in7(LUI_eq), .in8(jal_eq_1_eq), .in9(jalr_eq_1_eq), .in10(1'b0), .in11(1'b0), .in12(1'b0), .in13(1'b0),
    .in14(1'b0), .in15(1'b0), .num(priorityencoder_1_num));  // open: any
  ROM #(.AddrBits(4), .Bits(11)) rom_1 (
    .A(priorityencoder_1_num), .sel(1'b1), .D({WDsel, RFW, ALUSrcB, ALUSrcA, ALUOp, PCsel}));

  // Notes on the sheet:
  //   contents of rom_1 (hex, n*v repeats v):
  //   200,208,20c,210,240,24c,250,31c,761,641
endmodule
